// Logisim project my.circ as structural Verilog: 7 circuits, main circuit main
module main (
  input  in_1,
  input  in_2,
  input  in_3,
  input  in_4,
  input  in_5,
  input  in_6,
  input  in_7,
  input  in_8,
  input  in_9,
  input  in_10,
  input  in_11,
  input  in_12,
  input  in_13,
  input  in_14,
  input  in_15,
  input  in_16
);

  wire and_1_out, not_1_out, not_2_out, not_3_out, not_4_out;

  not not_1 (not_1_out, in_1);
  not not_2 (not_2_out, in_2);
  not not_3 (not_3_out, in_3);
  not not_4 (not_4_out, in_4);
  and and_1 (and_1_out, not_1_out, not_2_out, not_3_out, not_4_out);
  // AND_Gate and_2 has open pins: in0=in_1, in1=not_2_out, in2=not_3_out, in3=not_4_out, out=open
  // AND_Gate and_3 has open pins: in0=not_1_out, in1=in_2, in2=not_3_out, in3=not_4_out, out=open
  // AND_Gate and_4 has open pins: in0=in_1, in1=in_2, in2=not_3_out, in3=not_4_out, out=open
  // AND_Gate and_5 has open pins: in0=not_1_out, in1=not_2_out, in2=in_3, in3=not_4_out, out=open
  // AND_Gate and_6 has open pins: in0=in_1, in1=not_2_out, in2=in_3, in3=not_4_out, out=open
  // AND_Gate and_7 has open pins: in0=not_1_out, in1=in_2, in2=in_3, in3=not_4_out, out=open
  // AND_Gate and_8 has open pins: in0=in_1, in1=in_2, in2=in_3, in3=not_4_out, out=open
  // AND_Gate and_9 has open pins: in0=not_1_out, in1=not_2_out, in2=not_3_out, in3=in_4, out=open
  // AND_Gate and_10 has open pins: in0=in_1, in1=not_2_out, in2=not_3_out, in3=in_4, out=open
  // AND_Gate and_11 has open pins: in0=not_1_out, in1=in_2, in2=not_3_out, in3=in_4, out=open
  // AND_Gate and_12 has open pins: in0=in_1, in1=in_2, in2=not_3_out, in3=in_4, out=open
  // AND_Gate and_13 has open pins: in0=not_1_out, in1=not_2_out, in2=in_3, in3=in_4, out=open
  // AND_Gate and_14 has open pins: in0=in_1, in1=not_2_out, in2=in_3, in3=in_4, out=open
  // AND_Gate and_15 has open pins: in0=not_1_out, in1=in_2, in2=in_3, in3=in_4, out=open
  // AND_Gate and_16 has open pins: in0=in_1, in1=in_2, in2=in_3, in3=in_4, out=open
  registers registers_1 (
    .switch(and_1_out), .in_2(in_5), .in_3(in_6), .in_4(in_7), .in_5(in_9), .in_6(in_10), .in_7(in_11),
    .in_8(in_12), .in_9(in_13), .in_10(in_14), .in_11(in_15), .in_12(in_16));  // open: out_13, out_14, out_15, out_16, out_17, out_18, out_19, out_20
endmodule

module add_and_sub (
  input  switch,
  input  add_or_sub_switch,
  input  input_from_register,
  input  in_4,
  input  in_5,
  input  in_6,
  input  in_7,
  input  in_8,
  input  in_9,
  input  in_10,
  input  input_from_data,
  input  in_12,
  input  in_13,
  input  in_14,
  input  in_15,
  input  in_16,
  input  in_17,
  input  in_18,
  output out_19,
  output out_20,
  output out_21,
  output out_22,
  output out_23,
  output out_24,
  output out_25,
  output out_26,
  output out_27
);

  wire and_1_out, and_2_out, and_3_out, and_4_out, and_5_out, and_6_out, and_7_out, and_8_out, and_9_out,
       and_10_out, and_11_out, and_12_out, and_13_out, and_14_out, and_15_out, and_16_out, fadder_1_out_5,
       fadder_2_out_5, fadder_3_out_5, fadder_4_out_5, fadder_5_out_5, fadder_6_out_5, fadder_7_out_5,
       xor_1_out, xor_2_out, xor_3_out, xor_4_out, xor_5_out, xor_6_out, xor_7_out, xor_8_out;

  xor xor_1 (xor_1_out, add_or_sub_switch, input_from_data);
  xor xor_2 (xor_2_out, add_or_sub_switch, in_12);
  xor xor_3 (xor_3_out, add_or_sub_switch, in_13);
  xor xor_4 (xor_4_out, add_or_sub_switch, in_14);
  xor xor_5 (xor_5_out, add_or_sub_switch, in_15);
  xor xor_6 (xor_6_out, add_or_sub_switch, in_16);
  xor xor_7 (xor_7_out, add_or_sub_switch, in_17);
  xor xor_8 (xor_8_out, add_or_sub_switch, in_18);
  and and_1 (and_1_out, switch, input_from_register);
  and and_2 (and_2_out, switch, in_4);
  and and_3 (and_3_out, switch, in_5);
  and and_4 (and_4_out, switch, in_6);
  and and_5 (and_5_out, switch, in_7);
  and and_6 (and_6_out, switch, in_8);
  and and_7 (and_7_out, switch, in_9);
  and and_8 (and_8_out, switch, in_10);
  and and_9 (and_9_out, switch, xor_1_out);
  and and_10 (and_10_out, switch, xor_2_out);
  and and_11 (and_11_out, switch, xor_3_out);
  and and_12 (and_12_out, switch, xor_4_out);
  and and_13 (and_13_out, switch, xor_5_out);
  and and_14 (and_14_out, switch, xor_6_out);
  and and_15 (and_15_out, switch, xor_7_out);
  and and_16 (and_16_out, switch, xor_8_out);
  fadder fadder_1 (
    .in_1(add_or_sub_switch), .in_2(and_1_out), .in_3(and_9_out), .out_4(out_19), .out_5(fadder_1_out_5));
  fadder fadder_2 (.in_1(fadder_1_out_5), .in_2(and_2_out), .in_3(and_10_out), .out_4(out_20), .out_5(fadder_2_out_5));
  fadder fadder_3 (.in_1(fadder_2_out_5), .in_2(and_3_out), .in_3(and_11_out), .out_4(out_21), .out_5(fadder_3_out_5));
  fadder fadder_4 (.in_1(fadder_3_out_5), .in_2(and_4_out), .in_3(and_12_out), .out_4(out_22), .out_5(fadder_4_out_5));
  fadder fadder_5 (.in_1(fadder_4_out_5), .in_2(and_5_out), .in_3(and_13_out), .out_4(out_23), .out_5(fadder_5_out_5));
  fadder fadder_6 (.in_1(fadder_5_out_5), .in_2(and_6_out), .in_3(and_14_out), .out_4(out_24), .out_5(fadder_6_out_5));
  fadder fadder_7 (.in_1(fadder_6_out_5), .in_2(and_7_out), .in_3(and_15_out), .out_4(out_25), .out_5(fadder_7_out_5));
  fadder fadder_8 (.in_1(fadder_7_out_5), .in_2(and_8_out), .in_3(and_16_out), .out_4(out_26), .out_5(out_27));
endmodule

module hadder (
  input  a,
  input  b,
  output s,
  output c
);

  wire not_1_out, or_1_out;

  or or_1 (or_1_out, a, b);
  and and_1 (c, b, a);
  and and_2 (s, or_1_out, not_1_out);
  not not_1 (not_1_out, c);
endmodule

module fadder (
  input  in_1,
  input  in_2,
  input  in_3,
  output out_4,
  output out_5
);

  wire hadder_1_c, hadder_1_s, hadder_2_c;

  hadder hadder_1 (.a(in_2), .b(in_3), .s(hadder_1_s), .c(hadder_1_c));
  hadder hadder_2 (.a(in_1), .b(hadder_1_s), .s(out_4), .c(hadder_2_c));
  or or_1 (out_5, hadder_2_c, hadder_1_c);
endmodule

module ff (
  input  in_1,
  input  in_2,
  output out_3
);

  wire nand_1_out, nand_2_out, nand_4_out;

  nand nand_1 (nand_1_out, in_1, in_2);
  nand nand_2 (nand_2_out, nand_1_out, in_2);
  nand nand_3 (out_3, nand_1_out, nand_4_out);
  nand nand_4 (nand_4_out, out_3, nand_2_out);
endmodule

module r (
  input  switch,
  input  data,
  input  in_3,
  input  in_4,
  input  in_5,
  input  in_6,
  input  in_7,
  input  in_8,
  input  in_9,
  input  readswitch,
  output out_11,
  output out_12,
  output out_13,
  output out_14,
  output out_15,
  output out_16,
  output out_17,
  output out_18
);

  wire ff_1_out_3, ff_2_out_3, ff_3_out_3, ff_4_out_3, ff_5_out_3, ff_6_out_3, ff_7_out_3, ff_8_out_3;

  ff ff_1 (.in_1(data), .in_2(switch), .out_3(ff_1_out_3));
  ff ff_2 (.in_1(in_3), .in_2(switch), .out_3(ff_2_out_3));
  ff ff_3 (.in_1(in_4), .in_2(switch), .out_3(ff_3_out_3));
  ff ff_4 (.in_1(in_5), .in_2(switch), .out_3(ff_4_out_3));
  ff ff_5 (.in_1(in_6), .in_2(switch), .out_3(ff_5_out_3));
  ff ff_6 (.in_1(in_7), .in_2(switch), .out_3(ff_6_out_3));
  ff ff_7 (.in_1(in_8), .in_2(switch), .out_3(ff_7_out_3));
  ff ff_8 (.in_1(in_9), .in_2(switch), .out_3(ff_8_out_3));
  and and_1 (out_11, ff_1_out_3, readswitch);
  and and_2 (out_12, ff_2_out_3, readswitch);
  and and_3 (out_13, ff_3_out_3, readswitch);
  and and_4 (out_14, ff_4_out_3, readswitch);
  and and_5 (out_15, ff_5_out_3, readswitch);
  and and_6 (out_16, ff_6_out_3, readswitch);
  and and_7 (out_17, ff_7_out_3, readswitch);
  and and_8 (out_18, ff_8_out_3, readswitch);
endmodule

module registers (
  input  switch,
  input  in_2,
  input  in_3,
  input  in_4,
  input  in_5,
  input  in_6,
  input  in_7,
  input  in_8,
  input  in_9,
  input  in_10,
  input  in_11,
  input  in_12,
  output out_13,
  output out_14,
  output out_15,
  output out_16,
  output out_17,
  output out_18,
  output out_19,
  output out_20
);

  wire and_1_out, and_2_out, and_3_out, and_4_out, and_5_out, and_6_out, and_7_out, and_8_out, not_1_out,
       not_2_out, not_3_out, not_4_out;

  not not_1 (not_1_out, in_2);
  not not_2 (not_2_out, switch);
  not not_3 (not_3_out, in_3);
  not not_4 (not_4_out, in_4);
  and and_1 (and_1_out, not_1_out, not_3_out, not_4_out);
  and and_2 (and_2_out, in_2, not_3_out, not_4_out);
  and and_3 (and_3_out, not_1_out, in_3, not_4_out);
  and and_4 (and_4_out, in_2, in_3, not_4_out);
  and and_5 (and_5_out, not_1_out, not_3_out, in_4);
  and and_6 (and_6_out, in_2, not_3_out, in_4);
  and and_7 (and_7_out, not_1_out, in_3, in_4);
  and and_8 (and_8_out, in_2, in_3, in_4);
  r r_1 (
    .switch(and_1_out), .data(in_5), .in_3(in_6), .in_4(in_7), .in_5(in_8), .in_6(in_9), .in_7(in_10),
    .in_8(in_11), .in_9(in_12), .readswitch(not_2_out), .out_11(out_13), .out_12(out_14), .out_13(out_15),
    .out_14(out_16), .out_15(out_17), .out_16(out_18), .out_17(out_19), .out_18(out_20));
  r r_2 (
    .switch(and_2_out), .data(in_5), .in_3(in_6), .in_4(in_7), .in_5(in_8), .in_6(in_9), .in_7(in_10),
    .in_8(in_11), .in_9(in_12), .readswitch(not_2_out), .out_11(out_13), .out_12(out_14), .out_13(out_15),
    .out_14(out_16), .out_15(out_17), .out_16(out_18), .out_17(out_19), .out_18(out_20));
  r r_3 (
    .switch(and_3_out), .data(in_5), .in_3(in_6), .in_4(in_7), .in_5(in_8), .in_6(in_9), .in_7(in_10),
    .in_8(in_11), .in_9(in_12), .readswitch(not_2_out), .out_11(out_13), .out_12(out_14), .out_13(out_15),
    .out_14(out_16), .out_15(out_17), .out_16(out_18), .out_17(out_19), .out_18(out_20));
  r r_4 (
    .switch(and_4_out), .data(in_5), .in_3(in_6), .in_4(in_7), .in_5(in_8), .in_6(in_9), .in_7(in_10),
    .in_8(in_11), .in_9(in_12), .readswitch(not_2_out), .out_11(out_13), .out_12(out_14), .out_13(out_15),
    .out_14(out_16), .out_15(out_17), .out_16(out_18), .out_17(out_19), .out_18(out_20));
  r r_5 (
    .switch(and_5_out), .data(in_5), .in_3(in_6), .in_4(in_7), .in_5(in_8), .in_6(in_9), .in_7(in_10),
    .in_8(in_11), .in_9(in_12), .readswitch(not_2_out), .out_11(out_13), .out_12(out_14), .out_13(out_15),
    .out_14(out_16), .out_15(out_17), .out_16(out_18), .out_17(out_19), .out_18(out_20));
  r r_6 (
    .switch(and_6_out), .data(in_5), .in_3(in_6), .in_4(in_7), .in_5(in_8), .in_6(in_9), .in_7(in_10),
    .in_8(in_11), .in_9(in_12), .readswitch(not_2_out), .out_11(out_13), .out_12(out_14), .out_13(out_15),
    .out_14(out_16), .out_15(out_17), .out_16(out_18), .out_17(out_19), .out_18(out_20));
  r r_7 (
    .switch(and_7_out), .data(in_5), .in_3(in_6), .in_4(in_7), .in_5(in_8), .in_6(in_9), .in_7(in_10),
    .in_8(in_11), .in_9(in_12), .readswitch(not_2_out), .out_11(out_13), .out_12(out_14), .out_13(out_15),
    .out_14(out_16), .out_15(out_17), .out_16(out_18), .out_17(out_19), .out_18(out_20));
  r r_8 (
    .switch(and_8_out), .data(in_5), .in_3(in_6), .in_4(in_7), .in_5(in_8), .in_6(in_9), .in_7(in_10),
    .in_8(in_11), .in_9(in_12), .readswitch(not_2_out), .out_11(out_13), .out_12(out_14), .out_13(out_15),
    .out_14(out_16), .out_15(out_17), .out_16(out_18), .out_17(out_19), .out_18(out_20));
endmodule
